# Fritzing sketch Clock Controls (saved by Fritzing 0.9.3b)
breadboards: 1

parts:
  LCD1 = LCD screen
  Part1 = Arduino MKR1000
  R1 = Resistor [tolerance=±5% resistance=1k package="2512 [SMD]"]
  R2 = Trimmer Potentiometer [maximum_resistance=10kΩ package=THT]
  ENCODER1 = Rotary Encoder with Button Knob
  R3 = Resistor [tolerance=±5% resistance=10k package="2512 [SMD]"]

nets:
  VSS: LCD1.VSS, LCD1.R/W, LCD1.LED-, Part1.GND, R2.leg1, ENCODER1.C, ENCODER1.no_name_yet#5
  VDD: LCD1.VDD, Part1.5V, R1.Pin_0, R2.leg2, R3.Pin_1
  N1: LCD1.V0, R2.wiper
  N2: LCD1.RS, Part1.D0
  N3: LCD1.E, Part1.D1
  N4: LCD1.DB4, Part1.D2_PWM
  N5: LCD1.DB5, Part1.D3_PWM
  N6: LCD1.DB6, Part1.D4_PWM
  N7: LCD1.DB7, Part1.D5_PWM
  N8: LCD1.LED+, R1.Pin_1
  N9: Part1.D6, ENCODER1.no_name_yet#4, R3.Pin_0
  N10: Part1.D7, ENCODER1.B
  N11: Part1.D8_MOSI, ENCODER1.A

custom parts:
  Arduino MKR1000: MKR1000 is a powerful board that combines the functionality of the Zero and the Wi-Fi Shield. It is the ideal solution for makers wanting to design IoT projects with minimal previous experience in networking
  Rotary Encoder with Button Knob: Rotary Encoder with 1/4" Shaft and Knob
