# Fritzing sketch Glove MIDI sampler  (saved by Fritzing 0.9.3b)
breadboards: 1

parts:
  Part1 = Arduino MKR1000
  Part2 = Black Joystick KY-023
  R1 = 2.2 inch Basic Flex Resistor
  R2 = 2.2 inch Basic Flex Resistor
  R3 = 2.2 inch Basic Flex Resistor
  R4 = 2.2 inch Basic Flex Resistor
  R5 = 2.2 inch Basic Flex Resistor
  R6 = Resistor [tolerance=±5% resistance=470 package="0603 [SMD]"]
  R7 = Resistor [tolerance=±5% resistance=470 package="0603 [SMD]"]
  R8 = Resistor [tolerance=±5% resistance=470 package="0603 [SMD]"]
  R9 = Resistor [tolerance=±5% resistance=470 package="0603 [SMD]"]
  R10 = Resistor [tolerance=±5% resistance=470 package="0603 [SMD]"]

nets:
  N1: Part1.A0_DAC0, R5.Pin_2, R10.Pin_0
  N2: Part1.A1, R4.Pin_2, R9.Pin_0
  N3: Part1.A2, R3.Pin_2, R8.Pin_0
  N4: Part1.A3, R2.Pin_2, R7.Pin_0
  N5: Part1.A4, R1.Pin_2, R6.Pin_0
  N6: Part1.A5, Part2.VRx
  GND: Part1.GND, Part2.GND, R6.Pin_1, R7.Pin_1, R8.Pin_1, R9.Pin_1, R10.Pin_1
  5V: Part1.5V, Part2.+5V, R1.pin_1, R2.pin_1, R3.pin_1, R4.pin_1, R5.pin_1

custom parts:
  Arduino MKR1000: MKR1000 is a powerful board that combines the functionality of the Zero and the Wi-Fi Shield. It is the ideal solution for makers wanting to design IoT projects with minimal previous experience in networking
  Black Joystick KY-023: Description: The joystick is a combination of 2 analoog potentiometer and a digital switch. Arduino GND --> Module pin - Arduino +5V --> Module pin +5V Arduino Analoog 0 --> Module VRx Arduino Analoog 1 --> Module VRy Arduino Digital --> Module SW Dimensions: 1" x 1.25"
  2.2 inch Basic Flex Resistor: A generic Flex resistor - SparkFun: SEN-10264
