# Fritzing sketch Steering Wheel (saved by Fritzing 0.9.3b)
breadboards: 1

parts:
  Part1 = Arduino MKR1000
  Part2 = Adafruit LIS3DH [part_number="Adafruit #2809"]
  R1 = Resistor [tolerance=±5% resistance=220 package=THT]
  R2 = Resistor [tolerance=±5% resistance=220 package=THT]
  R3 = Resistor [tolerance=±5% resistance=220 package=THT]
  S1 = Round Pushbutton
  S2 = SWITCH-MOMENTARY-2 [package=tactile-switch-1101ne]
  S3 = Round Pushbutton

nets:
  N1: Part1.D4_PWM, R1.Pin_1, S1.leg0
  N2: Part1.D5_PWM, R2.Pin_1, S3.leg0
  N3: Part1.D6, R3.Pin_1, S2.2
  N4: Part1.D7, Part2.CS
  N5: Part1.D8_MOSI, Part2.SDA
  N6: Part1.D10_MISO, Part2.SDO
  N7: Part1.D12_SCL, Part2.SCL
  GND: Part1.GND, Part2.GND, R1.Pin_0, R2.Pin_0, R3.Pin_0
  5V: Part1.5V, Part2.VIN, S1.leg1, S2.1, S3.leg1

custom parts:
  Arduino MKR1000: MKR1000 is a powerful board that combines the functionality of the Zero and the Wi-Fi Shield. It is the ideal solution for makers wanting to design IoT projects with minimal previous experience in networking
  Adafruit LIS3DH: The LIS3DH is a very popular low power triple-axis accelerometer. It's low-cost, but has just about every 'extra' you'd want in an accelerometer: Three axis sensing, 10-bit precision ±2g/±4g/±8g/±16g selectable scaling Both I2C (2 possible addresses) and SPI interface options Interrupt output Multiple data rate options 1 Hz to 5Khz As low as 2uA current draw (just the chip itself, not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
